# Fritzing sketch MPL115A2 (saved by Fritzing 0.9.3b)
breadboards: 1

parts:
  부품1 = MPL115A2 I2C Barometric Pressure, Temperature Sensor
  Raspberry_Pi_1 = Raspberry Pi 3 [part_number=RPI-3-V1.2]

nets:
  VDD: 부품1.VDD, Raspberry_Pi_1.3v3
  GND: 부품1.GND, Raspberry_Pi_1.GND, Raspberry_Pi_1.GIPO18, Raspberry_Pi_1.GIPO15
  N1: 부품1.SCL, Raspberry_Pi_1.GPIO3
  N2: 부품1.SDA, Raspberry_Pi_1.GPIO2

custom parts:
  MPL115A2 I2C Barometric Pressure, Temperature Sensor: This pressure sensor from Freescale is a great low-cost sensing solution for measuring barometric pressure. At 1.5 hPa resolution, it's not as precise as our favorite pressure sensor, the BMP085, which has up to 0.03 hPa resolution so we don't suggest it as a precision altimeter. However, it's great for basic barometric pressure sensing. The sensor is soldered onto a PCB with 10K pull-up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
